# Fritzing sketch thermistor_v2 (saved by Fritzing 0.9.3b)
breadboards: 1

parts:
  SERIESRESISTOR = Resistor [tolerance=±5% resistance=120 package=THT]
  part = Arduino Uno (Rev3)
  THERMISTOR = Temperature Sensor (Thermistor) [thermistor_type=NTC package=THT]

nets:
  N1: SERIESRESISTOR.Pin_0, part.AREF, part.5V
  N2: SERIESRESISTOR.Pin_1, part.A1, THERMISTOR.pin_0
  N3: part.GND, THERMISTOR.pin_1
