# Fritzing sketch Selecting_RGB_LED (saved by Fritzing 0.9.3b)
circuit board: 8.46667cm x 5.64444cm
breadboards: 1

parts:
  LED1 = RGB LED (com. anode, rbg) [package="5 mm [THT]"]
  R1 = Resistor [tolerance=±5% resistance=220 package="2010 [SMD]"]
  Part1 = Arduino Uno (Rev3) - ICSP
  R2 = Rotary Potentiometer (Small) [maximum_resistance=100kΩ package=THT]
  S1 = Pushbutton [package="[THT]"]
  S3 = Pushbutton [package="[THT]"]
  S2 = Pushbutton [package="[THT]"]
  R3 = Resistor [tolerance=±5% resistance=10k package=THT]
  R6 = Resistor [tolerance=±5% resistance=10k package=THT]
  R7 = Resistor [tolerance=±5% resistance=10k package=THT]

nets:
  N1: LED1.red_cathode, Part1.D11_PWM/MOSI
  N2: LED1.common_anode, R1.Pin_1
  N3: LED1.blue_cathode, Part1.D10_PWM/SS
  N4: LED1.green_cathode, Part1.D9_PWM
  N5: R1.Pin_0, Part1.5V, R2.leg2, S1.Pin_3, S1.Pin_4, S3.Pin_3, S3.Pin_4, S2.Pin_3, S2.Pin_4
  N6: Part1.A0, R2.wiper
  N7: Part1.GND, R2.leg1, R3.Pin_1, R6.Pin_1, R7.Pin_1
  N8: Part1.D2, S3.Pin_1, S3.Pin_2, R7.Pin_0
  N9: Part1.D4, S2.Pin_1, S2.Pin_2, R6.Pin_0
  N10: Part1.D7, S1.Pin_1, S1.Pin_2, R3.Pin_0
