# Fritzing sketch Advanced_RGB_LED (saved by Fritzing 0.9.3b)
circuit board: 8.46667cm x 5.64444cm
breadboards: 1

parts:
  LED1 = RGB LED (com. anode, rbg) [package="5 mm [THT]"]
  R1 = Resistor [tolerance=±5% resistance=220 package="2010 [SMD]"]
  Part1 = Arduino Uno (Rev3) - ICSP
  R2 = Rotary Potentiometer (Small) [maximum_resistance=100kΩ package=THT]

nets:
  N1: LED1.red_cathode, Part1.D11_PWM/MOSI
  N2: LED1.common_anode, R1.Pin_1
  N3: LED1.blue_cathode, Part1.D10_PWM/SS
  N4: LED1.green_cathode, Part1.D9_PWM
  N5: R1.Pin_0, Part1.5V, R2.leg2
  N6: Part1.A0, R2.wiper
  N7: Part1.GND, R2.leg1
